// Logisim project t1.circ as structural Verilog: 19 circuits, main circuit main
module main (
  input  [7:0] in_1,
  input  [7:0] in_2,
  input  [2:0] _000___Add,
  output [7:0] out_4,
  output [7:0] out_5
);

  ALU alu_1 (
    .A(in_1), .B(in_2), .op(_000___Add), .Vout(out_5), .mult(out_4));  // open: parity, zero, negative, overflow

  // Notes on the sheet:
  //   001 - Sub
  //   010 - BCD Add
  //   011 - Mult
  //   100 - And
  //   101 - Or
  //   110 - Not
  //   111 - Xor
endmodule

module ALU (
  input  [7:0] A,
  input  [7:0] B,
  input  [2:0] op,
  output [7:0] Vout,
  output [7:0] mult,
  output parity,
  output zero,
  output negative,
  output overflow
);

  wire bcd_overflow, sub_overflow, sum_overflow;
  wire [7:0] and_out, bcdSum, mult_t, not_out, or_out, sub, sum, xor_out;

  add_8bit add_8bit_1 (.A(A), .B(B), .S(sum), .overflow(sum_overflow));
  sub_8bit sub_8bit_1 (.A(A), .B(B), .S(sub), .overflow(sub_overflow));
  BCDadd_8bit bcdadd_8bit_1 (.A(A), .B(B), .S(bcdSum), .Cout(bcd_overflow));
  mult_8bit mult_8bit_1 (.A(A), .B(B), .M0(mult_t), .M1(mult));
  and_8bit and_8bit_1 (.A(A), .B(B), .AandB(and_out));
  or_8bit or_8bit_1 (.A(A), .B(B), .AorB(or_out));
  not_8bit not_8bit_1 (.A(A), .notA(not_out));
  xor_8bit xor_8bit_1 (.A(A), .B(B), .AxorB(xor_out));
  Multiplexer #(.select(3), .width(8), .enable("false")) multiplexer_1 (
    .in0(sum), .in1(sub), .in2(bcdSum), .in3(mult_t), .in4(and_out), .in5(or_out), .in6(not_out),
    .in7(xor_out), .out(Vout), .sel(op));
  Multiplexer #(.select(2), .enable("false")) multiplexer_2 (
    .in0(sum_overflow), .in1(sub_overflow), .in2(bcd_overflow), .out(overflow), .sel(op[1:0]));  // open: in3
  parity_8bit parity_8bit_1 (.Vin(Vout), .parity(parity));
  zero_8bit zero_8bit_1 (.Vin(Vout), .zero(zero));
  negative_8bit negative_8bit_1 (.Vin(Vout), .negative(negative));

  // Other names for the same wires on the sheet: M1[7:0] = mult
endmodule

module add_8bit (
  input  [7:0] A,
  input  [7:0] B,
  output [7:0] S,
  output overflow
);

  wire cla_4bit_1_cout;

  CLA_4bit cla_4bit_1 (.A(A[3:0]), .B(B[3:0]), .S(S[3:0]), .Cout(cla_4bit_1_cout));  // open: Cin, PG, GG, overflow
  CLA_4bit cla_4bit_2 (
    .Cin(cla_4bit_1_cout), .A(A[7:4]), .B(B[7:4]), .S(S[7:4]), .overflow(overflow));  // open: PG, GG, Cout

  // Other names for the same wires on the sheet: A0[3:0] = A[3:0]; A1[3:0] = A[7:4]; B0[3:0] = B[3:0];
  //   B1[3:0] = B[7:4]
endmodule

module sub_8bit (
  input  [7:0] A,
  input  [7:0] B,
  output [7:0] S,
  output overflow
);

  wire cla_4bit_1_cout;
  wire [3:0] B0, B1;

  not_8bit not_8bit_1 (.A(B), .notA({B1, B0}));
  CLA_4bit cla_4bit_1 (.Cin(1'b1), .A(A[3:0]), .B(B0), .S(S[3:0]), .Cout(cla_4bit_1_cout));  // open: PG, GG, overflow
  CLA_4bit cla_4bit_2 (
    .Cin(cla_4bit_1_cout), .A(A[7:4]), .B(B1), .S(S[7:4]), .overflow(overflow));  // open: PG, GG, Cout

  // Other names for the same wires on the sheet: A0[3:0] = A[3:0]; A1[3:0] = A[7:4]
endmodule

module mult_8bit (
  input  [7:0] A,
  input  [7:0] B,
  output [7:0] M0,
  output [7:0] M1
);

  wire [15:0] bit_extender_1_out, cla_16bit_1_s, cla_16bit_2_s, cla_16bit_3_s, cla_16bit_4_s, cla_16bit_5_s,
       cla_16bit_6_s, sh0, sh1, sh2, sh3, sh4, sh5, sh6, sh7, shiftlr_16bit_1_vout, shiftlr_16bit_2_vout,
       shiftlr_16bit_3_vout, shiftlr_16bit_4_vout, shiftlr_16bit_5_vout, shiftlr_16bit_6_vout,
       shiftlr_16bit_7_vout;

  assign bit_extender_1_out = {{8{1'b0}}, A};  // Bit_Extender bit_extender_1
  Multiplexer #(.width(16), .enable("false")) multiplexer_1 (
    .in0({16{1'b0}}), .in1(bit_extender_1_out), .out(sh0), .sel(B[0]));
  shiftLR_16bit shiftlr_16bit_1 (.Vout(shiftlr_16bit_1_vout), .Vin(bit_extender_1_out));  // open: LR
  shiftLR_16bit shiftlr_16bit_2 (.Vout(shiftlr_16bit_2_vout), .Vin(shiftlr_16bit_1_vout));  // open: LR
  Multiplexer #(.width(16), .enable("false")) multiplexer_2 (
    .in1(shiftlr_16bit_1_vout), .out(sh1), .sel(B[1]));  // open: in0
  CLA_16bit cla_16bit_1 (.A(sh0), .B(sh1), .S(cla_16bit_1_s));  // open: Cin, PG, GG, Cout, overflow
  CLA_16bit cla_16bit_2 (.A(sh2), .B(sh3), .S(cla_16bit_2_s));  // open: Cin, PG, GG, Cout, overflow
  CLA_16bit cla_16bit_3 (.A(sh4), .B(sh5), .S(cla_16bit_3_s));  // open: Cin, PG, GG, Cout, overflow
  CLA_16bit cla_16bit_4 (.A(sh6), .B(sh7), .S(cla_16bit_4_s));  // open: Cin, PG, GG, Cout, overflow
  Multiplexer #(.width(16), .enable("false")) multiplexer_3 (
    .in0({16{1'b0}}), .in1(shiftlr_16bit_2_vout), .out(sh2), .sel(B[2]));
  shiftLR_16bit shiftlr_16bit_3 (.Vout(shiftlr_16bit_3_vout), .Vin(shiftlr_16bit_2_vout));  // open: LR
  CLA_16bit cla_16bit_5 (.A(cla_16bit_1_s), .B(cla_16bit_2_s), .S(cla_16bit_5_s));  // open: Cin, PG, GG, Cout, overflow
  CLA_16bit cla_16bit_6 (.A(cla_16bit_3_s), .B(cla_16bit_4_s), .S(cla_16bit_6_s));  // open: Cin, PG, GG, Cout, overflow
  Multiplexer #(.width(16), .enable("false")) multiplexer_4 (
    .in0({16{1'b0}}), .in1(shiftlr_16bit_3_vout), .out(sh3), .sel(B[3]));
  shiftLR_16bit shiftlr_16bit_4 (.Vout(shiftlr_16bit_4_vout), .Vin(shiftlr_16bit_3_vout));  // open: LR
  CLA_16bit cla_16bit_7 (.A(cla_16bit_5_s), .B(cla_16bit_6_s), .S({M1, M0}));  // open: Cin, PG, GG, Cout, overflow
  shiftLR_16bit shiftlr_16bit_5 (.Vout(shiftlr_16bit_5_vout), .Vin(shiftlr_16bit_4_vout));  // open: LR
  Multiplexer #(.width(16), .enable("false")) multiplexer_5 (
    .in0({16{1'b0}}), .in1(shiftlr_16bit_4_vout), .out(sh4), .sel(B[4]));
  Multiplexer #(.width(16), .enable("false")) multiplexer_6 (
    .in0({16{1'b0}}), .in1(shiftlr_16bit_5_vout), .out(sh5), .sel(B[5]));
  shiftLR_16bit shiftlr_16bit_6 (.Vout(shiftlr_16bit_6_vout), .Vin(shiftlr_16bit_5_vout));  // open: LR
  shiftLR_16bit shiftlr_16bit_7 (.Vout(shiftlr_16bit_7_vout), .Vin(shiftlr_16bit_6_vout));  // open: LR
  Multiplexer #(.width(16), .enable("false")) multiplexer_7 (
    .in0({16{1'b0}}), .in1(shiftlr_16bit_6_vout), .out(sh6), .sel(B[6]));
  Multiplexer #(.width(16), .enable("false")) multiplexer_8 (
    .in0({16{1'b0}}), .in1(shiftlr_16bit_7_vout), .out(sh7), .sel(B[7]));
endmodule

module BCDadd_8bit (
  input  [7:0] A,
  input  [7:0] B,
  output [7:0] S,
  output Cout
);

  wire bin2bcd_4bit_1_cout;
  wire [3:0] cla_4bit_1_s, cla_4bit_2_s;

  CLA_4bit cla_4bit_1 (.Cin(1'b0), .A(A[3:0]), .B(B[3:0]), .S(cla_4bit_1_s));  // open: PG, GG, Cout, overflow
  Bin2BCD_4bit bin2bcd_4bit_1 (.Bin(cla_4bit_1_s), .BCD(S[3:0]), .Cout(bin2bcd_4bit_1_cout));
  CLA_4bit cla_4bit_2 (
    .Cin(bin2bcd_4bit_1_cout), .A(A[7:4]), .B(B[7:4]), .S(cla_4bit_2_s));  // open: PG, GG, Cout, overflow
  Bin2BCD_4bit bin2bcd_4bit_2 (.Bin(cla_4bit_2_s), .BCD(S[7:4]), .Cout(Cout));

  // Other names for the same wires on the sheet: A0[3:0] = A[3:0]; A1[3:0] = A[7:4]; B0[3:0] = B[3:0];
  //   B1[3:0] = B[7:4]
endmodule

module Bin2BCD_4bit (
  input  [3:0] Bin,
  output [3:0] BCD,
  output Cout
);

  wire or_1_out;
  wire [3:0] cla_4bit_1_s;

  or or_1 (or_1_out, Bin[1], Bin[2]);
  and and_1 (Cout, or_1_out, Bin[3]);
  CLA_4bit cla_4bit_1 (.Cin(1'b0), .A(Bin), .B(4'b0110), .S(cla_4bit_1_s));  // open: PG, GG, Cout, overflow
  Multiplexer #(.width(4), .enable("false")) multiplexer_1 (.in0(Bin), .in1(cla_4bit_1_s), .out(BCD), .sel(Cout));
endmodule

module CLA_16bit (
  input  Cin,
  input  [15:0] A,
  input  [15:0] B,
  output [15:0] S,
  output PG,
  output GG,
  output Cout,
  output overflow
);

  wire C1, C2, C3, G0, G1, G2, G3, P0, P1, P2, P3;

  Pull_Resistor pull_resistor_1 (.node(Cin));
  CLA_4bit cla_4bit_1 (.Cin(Cin), .A(A[3:0]), .B(B[3:0]), .S(S[3:0]), .PG(P0), .GG(G0));  // open: Cout, overflow
  CLA_4bit cla_4bit_2 (.Cin(C1), .A(A[7:4]), .B(B[7:4]), .S(S[7:4]), .PG(P1), .GG(G1));  // open: Cout, overflow
  CLA_4bit cla_4bit_3 (.Cin(C2), .A(A[11:8]), .B(B[11:8]), .S(S[11:8]), .PG(P2), .GG(G2));  // open: Cout, overflow
  CLA_4bit cla_4bit_4 (.Cin(C3), .A(A[15:12]), .B(B[15:12]), .S(S[15:12]), .PG(P3), .GG(G3));  // open: Cout, overflow
  CLU_4in clu_4in_1 (
    .C0(Cin), .P0(P0), .P1(P1), .P2(P2), .P3(P3), .G0(G0), .G1(G1), .G2(G2), .G3(G3), .C1(C1), .C2(C2),
    .C3(C3), .C4(Cout), .PG(PG), .GG(GG), .overflow(overflow));

  // Other names for the same wires on the sheet: A0[3:0] = A[3:0]; A1[3:0] = A[7:4]; A2[3:0] = A[11:8];
  //   A3[3:0] = A[15:12]; B0[3:0] = B[3:0]; B1[3:0] = B[7:4]; B2[3:0] = B[11:8]; B3[3:0] = B[15:12]; C4 = Cout;
  //   S0[3:0] = S[3:0]; S1[3:0] = S[7:4]; S2[3:0] = S[11:8]; S3[3:0] = S[15:12]
endmodule

module CLA_4bit (
  input  Cin,
  input  [3:0] A,
  input  [3:0] B,
  output [3:0] S,
  output PG,
  output GG,
  output Cout,
  output overflow
);

  wire C1, C2, C3, G0, G1, G2, G3, P0, P1, P2, P3;

  Pull_Resistor pull_resistor_1 (.node(Cin));
  adder_1bit adder_1bit_1 (.C(Cin), .A(A[0]), .B(B[0]), .S(S[0]), .P(P0), .G(G0));
  adder_1bit adder_1bit_2 (.C(C1), .A(A[1]), .B(B[1]), .S(S[1]), .P(P1), .G(G1));
  adder_1bit adder_1bit_3 (.C(C2), .A(A[2]), .B(B[2]), .S(S[2]), .P(P2), .G(G2));
  adder_1bit adder_1bit_4 (.C(C3), .A(A[3]), .B(B[3]), .S(S[3]), .P(P3), .G(G3));
  CLU_4in clu_4in_1 (
    .C0(Cin), .P0(P0), .P1(P1), .P2(P2), .P3(P3), .G0(G0), .G1(G1), .G2(G2), .G3(G3), .C1(C1), .C2(C2),
    .C3(C3), .C4(Cout), .PG(PG), .GG(GG), .overflow(overflow));

  // Other names for the same wires on the sheet: C4 = Cout
endmodule

module CLU_4in (
  input  C0,
  input  P0,
  input  P1,
  input  P2,
  input  P3,
  input  G0,
  input  G1,
  input  G2,
  input  G3,
  output C1,
  output C2,
  output C3,
  output C4,
  output PG,
  output GG,
  output overflow
);

  wire and_1_out, and_2_out, and_3_out, and_4_out, and_5_out, and_6_out, and_8_out, and_9_out, and_10_out,
       and_11_out;

  Pull_Resistor pull_resistor_1 (.node(C0));
  and and_1 (and_1_out, C0, P0);
  or or_1 (C1, and_1_out, G0);
  and and_2 (and_2_out, C0, P0, P1);
  and and_3 (and_3_out, G0, P1);
  or or_2 (C2, and_2_out, and_3_out, G1);
  and and_4 (and_4_out, C0, P0, P1, P2);
  and and_5 (and_5_out, G0, P1, P2);
  and and_6 (and_6_out, G1, P2);
  or or_3 (C3, and_4_out, and_5_out, and_6_out, G2);
  and and_7 (PG, P0, P1, P2, P3);
  and and_8 (and_8_out, G0, P1, P2, P3);
  and and_9 (and_9_out, G1, P2, P3);
  and and_10 (and_10_out, G2, P3);
  xor xor_1 (overflow, C4, C3);
  or or_4 (GG, and_8_out, and_9_out, and_10_out, G3);
  and and_11 (and_11_out, C0, PG);
  or or_5 (C4, and_11_out, GG);

  // Notes on the sheet:
  //   Carry 1
  //   Carry 2
  //   Carry 3
endmodule

module adder_1bit (
  input  C,
  input  A,
  input  B,
  output S,
  output P,
  output G
);

  Pull_Resistor pull_resistor_1 (.node(C));
  xor xor_1 (P, A, B);
  xor xor_2 (S, C, P);
  and and_1 (G, A, B);
endmodule

module shiftLR_16bit (
  input  [15:0] Vin,
  input  LR,
  output [15:0] Vout
);

  Pull_Resistor pull_resistor_1 (.node(LR));
  Multiplexer #(.enable("false")) multiplexer_1 (.in0(Vin[14]), .in1(1'b0), .out(Vout[15]), .sel(LR));
  Multiplexer #(.enable("false")) multiplexer_2 (.in0(Vin[13]), .in1(Vin[15]), .out(Vout[14]), .sel(LR));
  Multiplexer #(.enable("false")) multiplexer_3 (.in0(Vin[12]), .in1(Vin[14]), .out(Vout[13]), .sel(LR));
  Multiplexer #(.enable("false")) multiplexer_4 (.in0(Vin[10]), .in1(Vin[12]), .out(Vout[11]), .sel(LR));
  Multiplexer #(.enable("false")) multiplexer_5 (.in0(Vin[11]), .in1(Vin[13]), .out(Vout[12]), .sel(LR));
  Multiplexer #(.enable("false")) multiplexer_6 (.in0(Vin[9]), .in1(Vin[11]), .out(Vout[10]), .sel(LR));
  Multiplexer #(.enable("false")) multiplexer_7 (.in0(Vin[8]), .in1(Vin[10]), .out(Vout[9]), .sel(LR));
  Multiplexer #(.enable("false")) multiplexer_8 (.in0(Vin[7]), .in1(Vin[9]), .out(Vout[8]), .sel(LR));
  Multiplexer #(.enable("false")) multiplexer_9 (.in0(Vin[5]), .in1(Vin[7]), .out(Vout[6]), .sel(LR));
  Multiplexer #(.enable("false")) multiplexer_10 (.in0(Vin[6]), .in1(Vin[8]), .out(Vout[7]), .sel(LR));
  Multiplexer #(.enable("false")) multiplexer_11 (.in0(Vin[4]), .in1(Vin[6]), .out(Vout[5]), .sel(LR));
  Multiplexer #(.enable("false")) multiplexer_12 (.in0(Vin[2]), .in1(Vin[4]), .out(Vout[3]), .sel(LR));
  Multiplexer #(.enable("false")) multiplexer_13 (.in0(Vin[3]), .in1(Vin[5]), .out(Vout[4]), .sel(LR));
  Multiplexer #(.enable("false")) multiplexer_14 (.in0(Vin[0]), .in1(Vin[2]), .out(Vout[1]), .sel(LR));
  Multiplexer #(.enable("false")) multiplexer_15 (.in0(Vin[1]), .in1(Vin[3]), .out(Vout[2]), .sel(LR));
  Multiplexer #(.enable("false")) multiplexer_16 (.in0(1'b0), .in1(Vin[1]), .out(Vout[0]), .sel(LR));

  // Other names for the same wires on the sheet: dir = LR; V0 = Vin[0]; V1 = Vin[1]; V2 = Vin[2]; V3 = Vin[3];
  //   V4 = Vin[4]; V5 = Vin[5]; V6 = Vin[6]; V7 = Vin[7]; V8 = Vin[8]; V9 = Vin[9]; V10 = Vin[10]; V11 = Vin[11];
  //   V12 = Vin[12]; V13 = Vin[13]; V14 = Vin[14]; V15 = Vin[15]
endmodule

module and_8bit (
  input  [7:0] A,
  input  [7:0] B,
  output [7:0] AandB
);

  and and_1 (AandB[0], A[0], B[0]);
  and and_2 (AandB[1], A[1], B[1]);
  and and_3 (AandB[2], A[2], B[2]);
  and and_4 (AandB[3], A[3], B[3]);
  and and_5 (AandB[4], A[4], B[4]);
  and and_6 (AandB[5], A[5], B[5]);
  and and_7 (AandB[6], A[6], B[6]);
  and and_8 (AandB[7], A[7], B[7]);
endmodule

module or_8bit (
  input  [7:0] A,
  input  [7:0] B,
  output [7:0] AorB
);

  or or_1 (AorB[0], A[0], B[0]);
  or or_2 (AorB[1], A[1], B[1]);
  or or_3 (AorB[2], A[2], B[2]);
  or or_4 (AorB[3], A[3], B[3]);
  or or_5 (AorB[4], A[4], B[4]);
  or or_6 (AorB[5], A[5], B[5]);
  or or_7 (AorB[6], A[6], B[6]);
  or or_8 (AorB[7], A[7], B[7]);
endmodule

module not_8bit (
  input  [7:0] A,
  output [7:0] notA
);

  not not_1 (notA[0], A[0]);
  not not_2 (notA[1], A[1]);
  not not_3 (notA[2], A[2]);
  not not_4 (notA[3], A[3]);
  not not_5 (notA[4], A[4]);
  not not_6 (notA[5], A[5]);
  not not_7 (notA[6], A[6]);
  not not_8 (notA[7], A[7]);
endmodule

module xor_8bit (
  input  [7:0] A,
  input  [7:0] B,
  output [7:0] AxorB
);

  xor xor_1 (AxorB[0], A[0], B[0]);
  xor xor_2 (AxorB[1], A[1], B[1]);
  xor xor_3 (AxorB[2], A[2], B[2]);
  xor xor_4 (AxorB[3], A[3], B[3]);
  xor xor_5 (AxorB[4], A[4], B[4]);
  xor xor_6 (AxorB[5], A[5], B[5]);
  xor xor_7 (AxorB[6], A[6], B[6]);
  xor xor_8 (AxorB[7], A[7], B[7]);
endmodule

module parity_8bit (
  input  [7:0] Vin,
  output parity
);

  wire xor_1_out, xor_2_out, xor_3_out, xor_4_out, xor_5_out, xor_6_out;

  xor xor_1 (xor_1_out, Vin[0], Vin[1]);
  xor xor_2 (xor_2_out, Vin[2], Vin[3]);
  xor xor_3 (xor_3_out, Vin[4], Vin[5]);
  xor xor_4 (xor_4_out, Vin[6], Vin[7]);
  xor xor_5 (xor_5_out, xor_1_out, xor_2_out);
  xor xor_6 (xor_6_out, xor_3_out, xor_4_out);
  xnor xnor_1 (parity, xor_5_out, xor_6_out);
endmodule

module zero_8bit (
  input  [7:0] Vin,
  output zero
);

  nor nor_1 (zero, Vin[0], Vin[1], Vin[2], Vin[3], Vin[5], Vin[6], Vin[7], Vin[4]);
endmodule

module negative_8bit (
  input  [7:0] Vin,
  output negative
);


  assign negative = Vin[7];
endmodule
