// Logisim project t2.circ as structural Verilog: 8 circuits, main circuit crc
module main (
);

  crc crc_1 ();  // open: polyn, msg_bit, load_polyn, clk, first_bit, R, crc_error

  // Notes on the sheet:
  //   32 bits menos significativos do polinomio
  //   Entrada da mensagem serial
  //   Sinal para ler o polinomio
  //   Sinal de primeiro bit da mensagem serial
  //   Reset assincrono do sistema
  //   Clock do sistema
  //   Sinal de erro apos 500 ciclos de clock
endmodule

module crc (
  input  [31:0] polyn,
  input  msg_bit,
  input  load_polyn,
  input  clk,
  input  first_bit,
  input  R,
  output crc_error
);

  wire and_1_out, d_ff_1_q, equals_1_v_out, nor_1_out, zero_1_not_zero;
  wire [31:0] calc_1_d, count_32bit_1_out_3, register_1_q;

  D_Flip_Flop d_ff_1 (.D(1'b1), .clk(and_1_out), .Q(d_ff_1_q), .reset(R));  // open: Qn, preset
  and and_1 (and_1_out, clk, first_bit);
  Register #(.width(32)) register_1 (.D(polyn), .en(1'b1), .clk(load_polyn), .Q(register_1_q));  // open: clr
  nor nor_1 (nor_1_out, first_bit, d_ff_1_q);
  calc calc_1 (.G(register_1_q), .\bit (msg_bit), .WE(1'b1), .clk(clk), .R(nor_1_out), .D(calc_1_d));
  count_32bit count_32bit_1 (.clk(clk), .R(nor_1_out), .out_3(count_32bit_1_out_3));  // open: count_out
  zero zero_1 (.v_in(calc_1_d), .not_zero(zero_1_not_zero));  // open: zero
  equals equals_1 (.A(count_32bit_1_out_3), .B(32'h1f4), .v_out(equals_1_v_out));
  and and_2 (crc_error, zero_1_not_zero, equals_1_v_out);

  // Notes on the sheet:
  //   polinomio
  //   500
endmodule

module bit_push (
  input  \bit ,
  input  [31:0] value,
  output [31:0] value_out
);


  assign value_out = {value[30:0], \bit };
endmodule

module calc (
  input  [31:0] G,
  input  \bit ,
  input  WE,
  input  clk,
  input  R,
  output [31:0] D
);

  wire and_1_out, d_ff_1_q;
  wire [31:0] bit_push_1_value_out, multiplexer_1_out, xor_1_out;

  Register #(.width(32)) register_1 (.D(bit_push_1_value_out), .en(WE), .clk(clk), .Q(D), .clr(R));
  and and_1 (and_1_out, clk, WE);
  D_Flip_Flop d_ff_1 (.D(D[31]), .clk(and_1_out), .Q(d_ff_1_q), .reset(R));  // open: Qn, preset
  assign xor_1_out = G ^ D;  // XOR_Gate xor_1, 32 bits wide
  Multiplexer #(.width(32), .enable("false")) multiplexer_1 (
    .in0(D), .in1(xor_1_out), .out(multiplexer_1_out), .sel(d_ff_1_q));
  bit_push bit_push_1 (.\bit (\bit ), .value(multiplexer_1_out), .value_out(bit_push_1_value_out));

  // Other names for the same wires on the sheet: rst = R
endmodule

module count_8bit (
  input  clk,
  input  R,
  output [7:0] value,
  output count_out
);

  wire t_ff_1_qn, t_ff_2_qn, t_ff_3_qn, t_ff_4_qn, t_ff_5_qn, t_ff_6_qn, t_ff_7_qn;

  T_Flip_Flop t_ff_1 (.T(1'b1), .clk(clk), .Q(value[0]), .Qn(t_ff_1_qn), .reset(R));  // open: preset
  T_Flip_Flop t_ff_2 (.T(1'b1), .clk(t_ff_1_qn), .Q(value[1]), .Qn(t_ff_2_qn), .reset(R));  // open: preset
  T_Flip_Flop t_ff_3 (.T(1'b1), .clk(t_ff_2_qn), .Q(value[2]), .Qn(t_ff_3_qn), .reset(R));  // open: preset
  T_Flip_Flop t_ff_4 (.T(1'b1), .clk(t_ff_3_qn), .Q(value[3]), .Qn(t_ff_4_qn), .reset(R));  // open: preset
  T_Flip_Flop t_ff_5 (.T(1'b1), .clk(t_ff_4_qn), .Q(value[4]), .Qn(t_ff_5_qn), .reset(R));  // open: preset
  T_Flip_Flop t_ff_6 (.T(1'b1), .clk(t_ff_5_qn), .Q(value[5]), .Qn(t_ff_6_qn), .reset(R));  // open: preset
  T_Flip_Flop t_ff_7 (.T(1'b1), .clk(t_ff_6_qn), .Q(value[6]), .Qn(t_ff_7_qn), .reset(R));  // open: preset
  T_Flip_Flop t_ff_8 (.T(1'b1), .clk(t_ff_7_qn), .Q(value[7]), .Qn(count_out), .reset(R));  // open: preset
endmodule

module count_32bit (
  input  clk,
  input  R,
  output [31:0] out_3,
  output count_out
);

  wire count_8bit_1_count_out, count_8bit_2_count_out, count_8bit_3_count_out;

  count_8bit count_8bit_1 (.clk(clk), .R(R), .value(out_3[7:0]), .count_out(count_8bit_1_count_out));
  count_8bit count_8bit_2 (
    .clk(count_8bit_1_count_out), .R(R), .value(out_3[15:8]), .count_out(count_8bit_2_count_out));
  count_8bit count_8bit_3 (
    .clk(count_8bit_2_count_out), .R(R), .value(out_3[23:16]), .count_out(count_8bit_3_count_out));
  count_8bit count_8bit_4 (.clk(count_8bit_3_count_out), .R(R), .value(out_3[31:24]), .count_out(count_out));
endmodule

module equals (
  input  [31:0] A,
  input  [31:0] B,
  output v_out
);

  wire [31:0] xor_1_out;

  assign xor_1_out = A ^ B;  // XOR_Gate xor_1, 32 bits wide
  zero zero_1 (.v_in(xor_1_out), .zero(v_out));  // open: not_zero
endmodule

module zero (
  input  [31:0] v_in,
  output zero,
  output not_zero
);

  or or_1 (not_zero, v_in[0], v_in[1], v_in[2], v_in[3], v_in[4], v_in[5], v_in[6], v_in[7], v_in[8], v_in[9], v_in[10], v_in[11], v_in[12], v_in[13], v_in[14], v_in[15], v_in[17], v_in[18], v_in[19], v_in[20], v_in[21], v_in[22], v_in[23], v_in[24], v_in[25], v_in[26], v_in[27], v_in[28], v_in[29], v_in[30], v_in[31], v_in[16]);
  not not_1 (zero, not_zero);
endmodule
